# Fritzing sketch PCB-SmartKettle (saved by Fritzing 0.9.3b)
circuit board: 5.07939cm x 5.04393cm

parts:
  Part1 = Arduino Nano (Rev3.0)
  Relé_plástico = songle relay
  J11 = female pin header, 3 pins [form="♀ (female)"]
  J12 = female pin header, 2 pins [form="♀ (female)"]
  J15 = female pin header, 2 pins [form="♀ (female)"]
  2N4401 = NPN-Transistor [package="TO92 [THT]"]
  1k = Resistor [tolerance=±5% resistance=1k package=THT]
  J14 = female pin header, 4 pins [form="♀ (female)"]
  J16 = female pin header, 2 pins [form="♀ (female)"]
  4_7K = Resistor [tolerance=±5% resistance=4.7k package=THT]

nets:
  N1: Part1.GND, J11.pin1, J11.pin3, J12.pin1, J15.pin1, 2N4401.E, J14.pin3, J16.pin2
  N2: Part1.D4, J16.pin1
  N3: Part1.D6, J11.pin2, 4_7K.Pin_1
  N4: Part1.D8, 1k.Pin_1
  N5: Part1.D11/MOSI, J14.pin1
  N6: Part1.D12/MISO, J14.pin2
  N7: Part1.VIN, J15.pin2
  5V: Part1.5V, Relé_plástico.VCC, J14.pin4, 4_7K.Pin_0
  N8: Relé_plástico.NO, J12.pin2
  N9: Relé_plástico.GND, 2N4401.C
  N10: 2N4401.B, 1k.Pin_0
